// Digital circuit Questão 2.30  item a.dig as structural Verilog
module \Questão_2_30__item_a  (
  input  a,
  input  b,
  input  c,
  output s
);

  wire and_1_out, and_2_out, not_1_out;

  not not_1 (not_1_out, a);
  and and_1 (and_1_out, not_1_out, b, c);
  and and_2 (and_2_out, a, b);
  or or_1 (s, and_1_out, and_2_out);
endmodule
