// Digital circuit Questão 2.30  item b.dig as structural Verilog
module \Questão_2_30__item_b  (
  input  a,
  input  b,
  output F
);

  wire not_1_out;

  not not_1 (not_1_out, a);
  and and_1 (F, not_1_out, b);
endmodule
