// Digital circuit Questão 2.30  item c.dig as structural Verilog
module \Questão_2_30__item_c  (
  input  a,
  input  b,
  input  c,
  output F
);

  wire and_1_out, and_2_out;

  and and_1 (and_1_out, a, b, c);
  and and_2 (and_2_out, a, b);
  or or_1 (F, and_1_out, c, a, b, and_2_out);
endmodule
