// Digital circuit Questão 2.54.dig as structural Verilog
module \Questão_2_54  (
  input  m0,
  input  m1,
  input  m2,
  output G
);

  wire and_1_out, and_2_out, and_3_out;

  and and_1 (and_1_out, ~m2, ~m1, m0);  // And
  and and_2 (and_2_out, ~m2, m1, ~m0);  // And
  and and_3 (and_3_out, m2, ~m1, ~m0);  // And
  or or_1 (G, and_1_out, and_2_out, and_3_out);
endmodule
