// Digital circuit Questão 7.22.dig as structural Verilog
module \Questão_7_22  (
  input  a,
  input  b,
  input  d,
  input  c,
  input  a_2,
  input  b_2,
  input  d_2,
  input  c_2,
  output F,
  output F_2
);

  wire and_1_out, and_2_out, and_3_out, and_4_out, and_5_out, and_6_out;

  and and_1 (and_1_out, ~a, b, d);  // And
  and and_2 (and_2_out, ~b, c, ~d);  // And
  or or_1 (F, and_1_out, and_2_out);
  and and_3 (and_3_out, b_2, d_2);
  and and_4 (and_4_out, ~b_2, ~d_2);  // And
  and and_5 (and_5_out, ~a_2, and_3_out);  // And
  and and_6 (and_6_out, and_4_out, c_2);
  or or_2 (F_2, and_5_out, and_6_out);
endmodule
