// Digital circuit Questão 7.23.dig as structural Verilog
module \Questão_7_23  (
  input  x,
  input  y,
  input  z,
  input  w,
  input  x_2,
  input  y_2,
  input  z_2,
  input  w_2,
  output F,
  output G,
  output F_2,
  output G_2
);

  wire and_1_out, and_2_out, and_3_out, and_4_out, and_5_out, and_7_out, and_8_out;

  and and_1 (and_1_out, ~x, y);  // And
  and and_2 (and_2_out, x, ~y, ~z);  // And
  and and_3 (and_3_out, ~w, ~x, y);  // And
  and and_4 (and_4_out, ~w, x, ~z);  // And
  or or_1 (F, and_1_out, and_2_out);
  or or_2 (G, and_3_out, and_4_out);
  and and_5 (and_5_out, ~x_2, y_2);  // And
  and and_6 (w_2, x_2, y_2, ~z_2);  // And
  and and_7 (and_7_out, and_5_out, ~w_2);  // And
  and and_8 (and_8_out, w_2, ~w_2);  // And
  or or_3 (F_2, and_5_out, w_2);
  or or_4 (G_2, and_7_out, and_8_out);
endmodule
