// Digital circuit Questão 7.24.dig as structural Verilog
module \Questão_7_24  (
  input  a,
  input  b,
  input  c,
  input  d,
  output F,
  output G
);

  wire and_1_out;

  and and_1 (and_1_out, a, b, c);
  or or_1 (F, and_1_out, d);
  not not_1 (G, a);
endmodule
